// Digital circuit Acc8_ovf.dig as structural Verilog
module Acc8_ovf (
  input  [7:0] A,
  input  en,
  input  rst,
  input  clk,
  output OVF,
  output [7:0] R
);

  wire [7:0] addsub8_ovf_1_r;

  AddSub8_ovf addsub8_ovf_1 (.A(A), .B(R), .AS(1'b0), .R(addsub8_ovf_1_r), .OVF(OVF));
  // Reg8 reg8_1: pin names not known; wires that end beside it: clk, addsub8_ovf_1_r, rst, en, R
endmodule
