// Digital circuit Add8.dig as structural Verilog
module Add8 (
  input  [7:0] A,
  input  [7:0] B,
  output [7:0] R,
  output C
);

  wire fa_2_co, fa_3_co, fa_4_co, fa_5_co, fa_6_co, fa_7_co, fa_8_co;

  FA fa_1 (.Ci(fa_2_co), .A(A[7]), .B(B[7]), .S(R[7]), .Co(C));
  FA fa_2 (.Ci(fa_3_co), .A(A[6]), .B(B[6]), .S(R[6]), .Co(fa_2_co));
  FA fa_3 (.Ci(fa_4_co), .A(A[5]), .B(B[5]), .S(R[5]), .Co(fa_3_co));
  FA fa_4 (.Ci(fa_5_co), .A(A[4]), .B(B[4]), .S(R[4]), .Co(fa_4_co));
  FA fa_5 (.Ci(fa_6_co), .A(A[3]), .B(B[3]), .S(R[3]), .Co(fa_5_co));
  FA fa_6 (.Ci(fa_7_co), .A(A[2]), .B(B[2]), .S(R[2]), .Co(fa_6_co));
  FA fa_7 (.Ci(fa_8_co), .A(A[1]), .B(B[1]), .S(R[1]), .Co(fa_7_co));
  FA fa_8 (.Ci(1'b0), .A(A[0]), .B(B[0]), .S(R[0]), .Co(fa_8_co));
endmodule
