// Digital circuit FA.dig as structural Verilog
module FA (
  input  Ci,
  input  A,
  input  B,
  output S,
  output Co
);

  wire and_1_out, and_2_out, and_3_out, and_4_out, and_5_out, and_6_out, and_7_out, not_1_out, not_2_out,
       not_3_out;

  not not_1 (not_1_out, Ci);
  not not_2 (not_2_out, A);
  not not_3 (not_3_out, B);
  and and_1 (and_1_out, not_2_out, B, not_1_out);
  and and_2 (and_2_out, A, not_3_out, not_1_out);
  and and_3 (and_3_out, not_2_out, not_3_out, Ci);
  and and_4 (and_4_out, A, B, Ci);
  and and_5 (and_5_out, A, B);
  and and_6 (and_6_out, A, Ci);
  and and_7 (and_7_out, B, Ci);
  or or_1 (S, and_1_out, and_2_out, and_3_out, and_4_out);
  or or_2 (Co, and_5_out, and_6_out, and_7_out);
endmodule
