// Digital circuit AddSub8.dig as structural Verilog
module AddSub8 (
  input  [7:0] A,
  input  AS,
  input  [7:0] B,
  output [7:0] R
);

  wire [7:0] multiplexer_1_out, reverse_cpl2_1_p2;

  // Reverse_CPL2 reverse_cpl2_1: pin names not known; wires that end beside it: B, reverse_cpl2_1_p2
  Multiplexer #(.Bits(8)) multiplexer_1 (.sel(AS), .in_0(B), .in_1(reverse_cpl2_1_p2), .out(multiplexer_1_out));
  Add8 add8_1 (.A(A), .B(multiplexer_1_out), .R(R));  // open: C
endmodule
