// Digital circuit Rev.dig as structural Verilog
module Rev (
  input  RI,
  input  I,
  output O,
  output RO
);

  wire and_1_out, and_2_out, not_1_out, not_2_out;

  not not_1 (not_1_out, RI);
  not not_2 (not_2_out, I);
  and and_1 (and_1_out, I, not_1_out);
  and and_2 (and_2_out, not_2_out, RI);
  or or_1 (RO, I, RI);
  or or_2 (O, and_1_out, and_2_out);
endmodule
