// Digital circuit Reverse-CPL2.dig as structural Verilog
module Reverse_CPL2 (
  input  [7:0] A,
  output [7:0] I
);

  wire [7:0] not_1_out;

  assign not_1_out = ~A;  // Not not_1, 8 bits wide
  Add8 add8_1 (.A(not_1_out), .B(8'h1), .R(I));  // open: C
  // Pins of 1 and 8 bits meet at I
endmodule
