// Digital circuit det-OVF.dig as structural Verilog
module det_OVF (
  input  sA,
  input  sB,
  input  sR,
  output OVF
);

  wire and_1_out, and_2_out, not_1_out, not_2_out, not_3_out;

  not not_1 (not_1_out, sA);
  not not_2 (not_2_out, sB);
  not not_3 (not_3_out, sR);
  and and_1 (and_1_out, not_1_out, not_2_out, sR);
  and and_2 (and_2_out, sA, sB, not_3_out);
  or or_1 (OVF, and_1_out, and_2_out);
endmodule
