// Digital circuit Acc8-seq.dig as structural Verilog
module Acc8_seq (
  input  CLK,
  input  en,
  input  rst,
  output [7:0] R,
  output OVF
);

  wire [3:0] counter_1_out;
  wire [7:0] rom_1_d;

  Counter #(.Bits(4)) counter_1 (.en(en), .C(CLK), .clr(rst), .out(counter_1_out));  // open: ovf
  ROM #(.AddrBits(4), .Bits(8)) rom_1 (.A(counter_1_out), .sel(1'b1), .D(rom_1_d));
  Acc8 acc8_1 (.A(rom_1_d), .en(en), .CLK(CLK), .rst(rst), .R(R), .OVF(OVF));

  // Notes on the sheet:
  //   contents of rom_1 (hex, n*v repeats v):
  //   1,2,3,2,5,6,7,8,9,a,b,c,d,e,f
endmodule
