// Digital circuit Acc8.dig as structural Verilog
module Acc8 (
  input  [7:0] A,
  input  en,
  input  CLK,
  input  rst,
  output [7:0] R,
  output OVF
);

  wire [7:0] reg8_1_p2;

  // Reg8 reg8_1: pin names not known; wires that end beside it: CLK, reg8_1_p2, rst, en, R
  AddSub8_ovf addsub8_ovf_1 (.A(R), .B(A), .AS(1'b0), .R(reg8_1_p2), .OVF(OVF));
endmodule
