// Digital circuit Acc8_.dig as structural Verilog
module Acc8 (
  input  [7:0] A,
  input  CLK,
  input  rst,
  output [7:0] R,
  output OVF
);

  wire reg8_1_p4, register_1_q;
  wire [7:0] reg8_1_p2;

  // Reg8 reg8_1: pin names not known; wires that end beside it: CLK, reg8_1_p2, rst, reg8_1_p4, R
  Register register_1 (.D(1'b1), .C(CLK), .en(OVF), .Q(register_1_q));
  AddSub8_ovf addsub8_ovf_1 (.A(R), .B(A), .AS(1'b0), .R(reg8_1_p2), .OVF(OVF));
  nor nor_1 (reg8_1_p4, register_1_q, OVF);
endmodule
