// Digital circuit AddSub8-ovf.dig as structural Verilog
module AddSub8_ovf (
  input  [7:0] A,
  input  [7:0] B,
  input  AS,
  output [7:0] R,
  output OVF
);

  wire [7:0] multiplexer_1_out, reverse_cpl2_1_p2;

  // Reverse_CPL2 reverse_cpl2_1: pin names not known; wires that end beside it: B, reverse_cpl2_1_p2
  Multiplexer #(.Bits(8)) multiplexer_1 (.sel(AS), .in_0(B), .in_1(reverse_cpl2_1_p2), .out(multiplexer_1_out));
  Add8 add8_1 (.A(A), .B(multiplexer_1_out), .R(R));  // open: C
  det_OVF det_ovf_1 (.sA(A[7]), .sB(multiplexer_1_out[7]), .sR(R[7]), .OVF(OVF));
endmodule
