// Digital circuit smem.dig as structural Verilog
module smem (
  input  [7:0] ADDR,
  input  en,
  output [7:0] DATA
);

  wire dec2_4_1_p3, dec2_4_1_p4, dec2_4_1_p5, dec2_4_1_p6;

  // dec2_4 dec2_4_1: pin names not known; wires that end beside it: ADDR[7:6], en, dec2_4_1_p3, dec2_4_1_p4, dec2_4_1_p5, dec2_4_1_p6, dec2_4_1_p4, dec2_4_1_p6
  // Probe addr1 on ADDR[5:0]
  // Probe addr2 on ADDR[4:0]
  ROM #(.AddrBits(6), .Bits(8)) ROM1 (.A(ADDR[5:0]), .sel(dec2_4_1_p3), .D(DATA));
  ROM #(.AddrBits(5), .Bits(8)) ROM2 (.A(ADDR[4:0]), .sel(dec2_4_1_p5), .D(DATA));

  // Notes on the sheet:
  //   contents of ROM1 (hex, n*v repeats v):
  //   0,1,2,3,4,5,6,7,ff,ff,ff,ff,ff,ff,ff,ff
  //   contents of ROM2 (hex, n*v repeats v):
  //   1,fe,2,fe,3,fe,0,ff
  //   ROM1 has a capacity of 64B
  //   addr: 00XXXXXX (0x00-0x3F)
  //   ROM2 has a capacity of 32B
  //   addr: 10XXXXXX (0x80-0xBF)
endmodule
