// Digital circuit bitcount2.dig as structural Verilog
module bitcount2 (
  input  [3:0] X,
  output [2:0] F
);

  wire and_2_out, and_3_out, and_4_out, and_5_out, and_6_out, and_7_out, and_8_out, and_9_out, and_10_out,
       and_11_out, and_12_out, and_13_out, and_14_out, and_15_out, not_1_out, not_2_out, not_3_out, not_4_out;

  not not_1 (not_1_out, X[3]);
  not not_2 (not_2_out, X[2]);
  not not_3 (not_3_out, X[1]);
  not not_4 (not_4_out, X[0]);
  and and_1 (F[2], X[0], X[1], X[2], X[3]);
  and and_2 (and_2_out, X[0], X[1], not_2_out);
  and and_3 (and_3_out, not_4_out, X[1], X[2]);
  and and_4 (and_4_out, X[0], not_3_out, X[3]);
  and and_5 (and_5_out, not_4_out, X[1], X[3]);
  and and_6 (and_6_out, X[0], X[2], not_1_out);
  and and_7 (and_7_out, not_4_out, X[2], X[3]);
  and and_8 (and_8_out, X[0], not_3_out, not_2_out, not_1_out);
  and and_9 (and_9_out, not_4_out, X[1], not_2_out, not_1_out);
  and and_10 (and_10_out, not_4_out, not_3_out, X[2], not_1_out);
  and and_11 (and_11_out, X[0], X[1], X[2], not_1_out);
  and and_12 (and_12_out, not_4_out, not_3_out, not_2_out, X[3]);
  and and_13 (and_13_out, X[0], X[1], not_2_out, X[3]);
  and and_14 (and_14_out, X[0], not_3_out, X[2], X[3]);
  and and_15 (and_15_out, not_4_out, X[1], X[2], X[3]);
  or or_1 (F[1], and_2_out, and_3_out, and_4_out, and_5_out, and_6_out, and_7_out);
  or or_2 (F[0], and_8_out, and_9_out, and_10_out, and_11_out, and_12_out, and_13_out, and_14_out, and_15_out);
endmodule
