// Digital circuit detect.dig as structural Verilog
module detect (
  input  A,
  input  B,
  input  C,
  input  D,
  output F
);

  wire and_1_out, nor_1_out;

  and and_1 (and_1_out, A, B, C, D);
  nor nor_1 (nor_1_out, D, C, B, A);
  or or_1 (F, and_1_out, nor_1_out);
endmodule
